# Fritzing sketch perfboard-layout (saved by Fritzing 1.0.8)
perfboards: 1

parts:
  U1 = Mini-360 DC-DC Buck converter [package=THT]
  A2 = ESP32 38Pin narrow
  A3 = usbc to 12V module
  R3 = Resistor [tolerance=±5% power=0.5W resistance=10k package=THT]
  F1 = Fan - 4 wire [package=THT]
  J1 = female pin header, 4 pins [form="♀ (female)"]
  J2 = female pin header, 4 pins [form="♀ (female)"]  # not connected
  Grove1 = Grove OLED 128x96
  R1 = Resistor [tolerance=±5% power=0.5W resistance=10k package=THT]

nets:
  N1: U1.IN+, A3.Pin_3, A3.Pin_4, F1.Power
  N2: U1.OUT+, A2.Pin_19, R1.Pin_1
  N3: A2.Pin_1, R3.Pin_1, Grove1.VCC
  N4: A2.Pin_5, R3.Pin_0, F1.Tach, J1.pin2
  N5: A2.Pin_9, F1.PWM, J1.pin1, R1.Pin_0
  GND: A2.Pin_14, A2.Pin_32, A2.Pin_38, F1.GND, J1.pin4, Grove1.GND
  N6: A2.Pin_33, Grove1.SDA
  N7: A2.Pin_36, Grove1.SCL
  N8: A3.Pin_1, A3.Pin_2

custom parts:
  Mini-360 DC-DC Buck converter: Mini-360 DC-DC Buck converter. Tiny buck step down voltage converter, input voltage 4.75 to 23V output 1 to 17V adjustable. Available from ebay and the like.
  ESP32 38Pin narrow: ESP32 38Pin narrow.
  usbc to 12V module: usbc to 12V module.
  Fan - 4 wire: Fan, 4 wire with tach.
