# Fritzing sketch perfboard-layout (saved by Fritzing 1.0.8)
circuit board: 8.46667cm x 5.64444cm
perfboards: 1

parts:
  A1 = ESP32 38Pin narrow
  U1 = Mini-360 DC-DC Buck converter [package=THT]
  A2 = usbc to 12V module
  J1 = female pin header, 4 pins [form="♀ (female)"]
  J2 = female pin header, 4 pins [form="♀ (female)"]
  Grove1 = Grove OLED 128x96
  F1 = Fan - 4 wire [package=THT]
  R2 = Resistor [tolerance=±5% power=0.25W resistance=10k package=THT]
  R3 = Resistor [tolerance=±5% power=0.25W resistance=10k package=THT]

nets (from the breadboard view):
  N1: A1.Pin_1, J2.pin3, Grove1.VCC, R3.Pin_1
  N2: A1.Pin_5, J1.pin2, F1.Tach, R3.Pin_0
  N3: A1.Pin_9, J1.pin1, F1.PWM, R2.Pin_1
  GND: A1.Pin_14, A1.Pin_32, A1.Pin_38, U1.IN-, U1.OUT-, A2.Pin_1, A2.Pin_2, J1.pin4, J2.pin4, Grove1.GND, F1.GND
  N4: A1.Pin_19, U1.OUT+, R2.Pin_0
  N5: A1.Pin_33, J2.pin2, Grove1.SDA
  N6: A1.Pin_36, J2.pin1, Grove1.SCL
  N7: U1.IN+, A2.Pin_3, A2.Pin_4, J1.pin3, F1.Power

custom parts:
  ESP32 38Pin narrow: ESP32 38Pin narrow.
  Mini-360 DC-DC Buck converter: Mini-360 DC-DC Buck converter. Tiny buck step down voltage converter, input voltage 4.75 to 23V output 1 to 17V adjustable. Available from ebay and the like.
  usbc to 12V module: usbc to 12V module.
  Fan - 4 wire: Fan, 4 wire with tach.
